// Logisim project Proj1313.circ as structural Verilog: 5 circuits, main circuit Arch
module Arch (
  input  [7:0] A,
  input  [7:0] B,
  input  [2:0] opcode,
  output [7:0] O,
  output Cout
);

  ALU alu_1 (.A(A), .B(B), .opcode(opcode), .O(O), .Cout(Cout));
endmodule

module ALU (
  input  [7:0] A,
  input  [7:0] B,
  input  [2:0] opcode,
  output [7:0] O,
  output Cout
);
endmodule

module addr8bit (
  input  [7:0] a,
  input  [7:0] b,
  input  cin,
  output [7:0] SumOA,
  output cout
);

  wire addr4bitoa_1_p5;

  // Addr4bitOA addr4bitoa_1: pin names not known; wires that end beside it: a[3:0], b[3:0], cin, SumOA[3:0], addr4bitoa_1_p5
  // Addr4bitOA addr4bitoa_2: pin names not known; wires that end beside it: a[7:4], b[7:4], addr4bitoa_1_p5, SumOA[7:4], cout
endmodule

module shift8bit (
  input  [7:0] b,
  output [7:0] Outp
);

  wire and_1_out, and_2_out, and_3_out, and_4_out, and_5_out, and_6_out, and_7_out, and_8_out, and_9_out,
       and_10_out, and_11_out, and_12_out, and_13_out, and_14_out, and_15_out, and_16_out;

  and and_1 (and_1_out, 1'b0, 1'b1);
  xor xor_1 (Outp[7], and_1_out, and_2_out);
  and and_2 (and_2_out, b[7], ~1'b1);  // AND_Gate
  and and_3 (and_3_out, b[7], 1'b1);
  xor xor_2 (Outp[6], and_3_out, and_4_out);
  and and_4 (and_4_out, b[6], ~1'b1);  // AND_Gate
  and and_5 (and_5_out, b[6], 1'b1);
  xor xor_3 (Outp[5], and_5_out, and_6_out);
  and and_6 (and_6_out, b[5], ~1'b1);  // AND_Gate
  and and_7 (and_7_out, b[5], 1'b1);
  xor xor_4 (Outp[4], and_7_out, and_8_out);
  and and_8 (and_8_out, b[4], ~1'b1);  // AND_Gate
  and and_9 (and_9_out, b[4], 1'b1);
  xor xor_5 (Outp[3], and_9_out, and_10_out);
  and and_10 (and_10_out, b[3], ~1'b1);  // AND_Gate
  and and_11 (and_11_out, b[3], 1'b1);
  xor xor_6 (Outp[2], and_11_out, and_12_out);
  and and_12 (and_12_out, b[2], ~1'b1);  // AND_Gate
  and and_13 (and_13_out, b[2], 1'b1);
  xor xor_7 (Outp[1], and_13_out, and_14_out);
  and and_14 (and_14_out, b[1], ~1'b1);  // AND_Gate
  and and_15 (and_15_out, b[1], 1'b1);
  and and_16 (and_16_out, b[0], ~1'b1);  // AND_Gate
  xor xor_8 (Outp[0], and_15_out, and_16_out);
endmodule

module MUX8x1 (
  input  I0,
  input  I1,
  input  I2,
  input  I3,
  input  I4,
  input  I5,
  input  I6,
  input  I7,
  input  S2,
  input  S1,
  input  S0,
  output Outp
);

  wire and_1_out, and_2_out, and_3_out, and_4_out, and_5_out, and_6_out, and_7_out, and_8_out;

  and and_1 (and_1_out, I0, ~S2, ~S1, ~S0);  // AND_Gate
  and and_2 (and_2_out, I1, ~S2, ~S1, S0);  // AND_Gate
  and and_3 (and_3_out, I2, ~S2, S1, ~S0);  // AND_Gate
  and and_4 (and_4_out, I3, ~S2, S1, S0);  // AND_Gate
  and and_5 (and_5_out, I4, S2, ~S1, ~S0);  // AND_Gate
  and and_6 (and_6_out, I5, S2, ~S1, S0);  // AND_Gate
  and and_7 (and_7_out, I6, S2, S1, ~S0);  // AND_Gate
  and and_8 (and_8_out, I7, S2, S1, S0);
  or or_1 (Outp, and_1_out, and_2_out, and_3_out, and_4_out, and_5_out, and_6_out, and_7_out, and_8_out);
endmodule
